// Logisim project Multiplicador4Bits.circ as structural Verilog: 1 circuit, main circuit main
module main (
  input  in_1,
  input  in_2,
  input  in_3,
  input  x,
  input  in_5,
  input  in_6,
  input  in_7,
  input  in_8,
  output out_9,
  output out_10,
  output out_11,
  output out_12,
  output out_13,
  output out_14,
  output out_15,
  output out_16
);

  wire adder_1_cout, adder_2_cout, adder_2_out, adder_3_cout, adder_3_out, adder_4_cout, adder_4_out,
       adder_5_cout, adder_6_cout, adder_6_out, adder_7_cout, adder_7_out, adder_8_cout, adder_8_out,
       adder_9_cout, adder_10_cout, adder_11_cout, and_2_out, and_3_out, and_4_out, and_5_out, and_6_out,
       and_7_out, and_8_out, and_9_out, and_10_out, and_11_out, and_12_out, and_13_out, and_14_out,
       and_15_out, and_16_out;

  and and_1 (out_16, x, in_8);
  and and_2 (and_2_out, in_3, in_8);
  and and_3 (and_3_out, x, in_7);
  and and_4 (and_4_out, in_2, in_8);
  and and_5 (and_5_out, in_3, in_7);
  and and_6 (and_6_out, in_1, in_8);
  and and_7 (and_7_out, in_2, in_7);
  and and_8 (and_8_out, in_1, in_7);
  and and_9 (and_9_out, in_1, in_6);
  Adder #(.width(1)) adder_1 (.a(and_2_out), .b(and_3_out), .out(out_15), .cin(1'b0), .cout(adder_1_cout));
  Adder #(.width(1)) adder_2 (.a(and_4_out), .b(and_5_out), .out(adder_2_out), .cin(adder_1_cout), .cout(adder_2_cout));
  Adder #(.width(1)) adder_3 (.a(and_6_out), .b(and_7_out), .out(adder_3_out), .cin(adder_2_cout), .cout(adder_3_cout));
  Adder #(.width(1)) adder_4 (.a(adder_3_cout), .b(and_8_out), .out(adder_4_out), .cin(1'b0), .cout(adder_4_cout));
  and and_10 (and_10_out, x, in_6);
  and and_11 (and_11_out, in_1, in_5);
  Adder #(.width(1)) adder_5 (.a(adder_2_out), .b(and_10_out), .out(out_14), .cin(1'b0), .cout(adder_5_cout));
  Adder #(.width(1)) adder_6 (
    .a(adder_3_out), .b(and_12_out), .out(adder_6_out), .cin(adder_5_cout), .cout(adder_6_cout));
  and and_12 (and_12_out, in_3, in_6);
  Adder #(.width(1)) adder_7 (
    .a(adder_4_out), .b(and_13_out), .out(adder_7_out), .cin(adder_6_cout), .cout(adder_7_cout));
  and and_13 (and_13_out, in_2, in_6);
  Adder #(.width(1)) adder_8 (
    .a(adder_4_cout), .b(and_9_out), .out(adder_8_out), .cin(adder_7_cout), .cout(adder_8_cout));
  and and_14 (and_14_out, x, in_5);
  and and_15 (and_15_out, in_3, in_5);
  Adder #(.width(1)) adder_9 (.a(adder_6_out), .b(and_14_out), .out(out_13), .cin(1'b0), .cout(adder_9_cout));
  Adder #(.width(1)) adder_10 (.a(adder_7_out), .b(and_15_out), .out(out_12), .cin(adder_9_cout), .cout(adder_10_cout));
  and and_16 (and_16_out, in_2, in_5);
  Adder #(.width(1)) adder_11 (
    .a(adder_8_out), .b(and_16_out), .out(out_11), .cin(adder_10_cout), .cout(adder_11_cout));
  Adder #(.width(1)) adder_12 (.a(adder_8_cout), .b(and_11_out), .out(out_10), .cin(adder_11_cout), .cout(out_9));

  // Other names for the same wires on the sheet: x0 = x; x1 = in_3; x2 = in_2; x3 = in_1; y0 = in_8; y1 = in_7;
  //   y2 = in_6; y3 = in_5

  // Notes on the sheet:
  //   =
endmodule
