// Logisim project memoria_5x8.circ as structural Verilog
module decodeer (
  input  a,
  input  b,
  input  c,
  output zero,
  output um,
  output dois,
  output tres,
  output quatro,
  output cinco,
  output seis,
  output sete
);

  wire not_1_out, not_2_out, not_3_out;

  not not_1 (not_1_out, a);
  not not_2 (not_2_out, b);
  not not_3 (not_3_out, c);
  and and_1 (zero, not_3_out, not_2_out, not_1_out);
  and and_2 (um, c, not_2_out, not_1_out);
  and and_3 (dois, not_3_out, b, not_1_out);
  and and_4 (tres, c, b, not_1_out);
  and and_5 (quatro, not_3_out, not_2_out, a);
  and and_6 (cinco, c, not_2_out, a);
  and and_7 (seis, not_3_out, b, a);
  and and_8 (sete, c, b, a);
endmodule

module memoria8x5 (
  input  in_1,
  input  in_2,
  input  in_3,
  input  in_4,
  input  in_5,
  input  a2,
  input  a1,
  input  a0,
  input  clk,
  input  read,
  input  write,
  output out_12,
  output out_13,
  output out_14,
  output out_15,
  output out_16
);

  wire and_1_out, and_2_out, and_3_out, and_4_out, and_5_out, and_6_out, and_7_out, and_8_out, and_9_out,
       decodeer_1_cinco, decodeer_1_dois, decodeer_1_quatro, decodeer_1_seis, decodeer_1_sete,
       decodeer_1_tres, decodeer_1_um, decodeer_1_zero;

  decodeer decodeer_1 (
    .a(a2), .b(a1), .c(a0), .zero(decodeer_1_zero), .um(decodeer_1_um), .dois(decodeer_1_dois),
    .tres(decodeer_1_tres), .quatro(decodeer_1_quatro), .cinco(decodeer_1_cinco), .seis(decodeer_1_seis),
    .sete(decodeer_1_sete));
  and and_1 (and_1_out, clk, read);
  and and_2 (and_2_out, decodeer_1_zero, and_1_out);
  and and_3 (and_3_out, decodeer_1_um, and_1_out);
  and and_4 (and_4_out, decodeer_1_dois, and_1_out);
  and and_5 (and_5_out, decodeer_1_tres, and_1_out);
  and and_6 (and_6_out, decodeer_1_quatro, and_1_out);
  and and_7 (and_7_out, decodeer_1_cinco, and_1_out);
  and and_8 (and_8_out, decodeer_1_seis, and_1_out);
  and and_9 (and_9_out, decodeer_1_sete, and_1_out);
  D_Flip_Flop d_ff_1 (.clk(and_2_out));  // open: D, Q, Qn, preset, reset
  D_Flip_Flop d_ff_2 (.clk(and_3_out));  // open: D, Q, Qn, preset, reset
  D_Flip_Flop d_ff_3 ();  // open: clk, D, Q, Qn, preset, reset
  D_Flip_Flop d_ff_4 ();  // open: clk, D, Q, Qn, preset, reset
  D_Flip_Flop d_ff_5 ();  // open: clk, D, Q, Qn, preset, reset
  D_Flip_Flop d_ff_6 ();  // open: clk, D, Q, Qn, preset, reset
  D_Flip_Flop d_ff_7 ();  // open: clk, D, Q, Qn, preset, reset
  D_Flip_Flop d_ff_8 ();  // open: clk, D, Q, Qn, preset, reset
  D_Flip_Flop d_ff_9 (.clk(and_2_out));  // open: D, Q, Qn, preset, reset
  D_Flip_Flop d_ff_10 (.clk(and_3_out));  // open: D, Q, Qn, preset, reset
  D_Flip_Flop d_ff_11 ();  // open: clk, D, Q, Qn, preset, reset
  D_Flip_Flop d_ff_12 ();  // open: clk, D, Q, Qn, preset, reset
  D_Flip_Flop d_ff_13 ();  // open: clk, D, Q, Qn, preset, reset
  D_Flip_Flop d_ff_14 ();  // open: clk, D, Q, Qn, preset, reset
  D_Flip_Flop d_ff_15 ();  // open: clk, D, Q, Qn, preset, reset
  D_Flip_Flop d_ff_16 ();  // open: clk, D, Q, Qn, preset, reset
  // D_Flip_Flop d_ff_17: pin names not known; wires that end beside it: in_3, and_2_out, in_4
  D_Flip_Flop d_ff_18 (.clk(and_3_out));  // open: D, Q, Qn, preset, reset
  D_Flip_Flop d_ff_19 ();  // open: clk, D, Q, Qn, preset, reset
  D_Flip_Flop d_ff_20 ();  // open: clk, D, Q, Qn, preset, reset
  D_Flip_Flop d_ff_21 ();  // open: clk, D, Q, Qn, preset, reset
  D_Flip_Flop d_ff_22 ();  // open: clk, D, Q, Qn, preset, reset
  D_Flip_Flop d_ff_23 ();  // open: clk, D, Q, Qn, preset, reset
  D_Flip_Flop d_ff_24 ();  // open: clk, D, Q, Qn, preset, reset
  D_Flip_Flop d_ff_25 (.clk(and_3_out));  // open: D, Q, Qn, preset, reset
  D_Flip_Flop d_ff_26 ();  // open: clk, D, Q, Qn, preset, reset
  D_Flip_Flop d_ff_27 ();  // open: clk, D, Q, Qn, preset, reset
  D_Flip_Flop d_ff_28 ();  // open: clk, D, Q, Qn, preset, reset
  D_Flip_Flop d_ff_29 ();  // open: clk, D, Q, Qn, preset, reset
  D_Flip_Flop d_ff_30 ();  // open: clk, D, Q, Qn, preset, reset
  D_Flip_Flop d_ff_31 ();  // open: clk, D, Q, Qn, preset, reset
  D_Flip_Flop d_ff_32 (.clk(and_2_out));  // open: D, Q, Qn, preset, reset
  D_Flip_Flop d_ff_33 (.clk(and_2_out));  // open: D, Q, Qn, preset, reset
  D_Flip_Flop d_ff_34 (.clk(and_3_out));  // open: D, Q, Qn, preset, reset
  D_Flip_Flop d_ff_35 ();  // open: clk, D, Q, Qn, preset, reset
  D_Flip_Flop d_ff_36 ();  // open: clk, D, Q, Qn, preset, reset
  D_Flip_Flop d_ff_37 ();  // open: clk, D, Q, Qn, preset, reset
  D_Flip_Flop d_ff_38 ();  // open: clk, D, Q, Qn, preset, reset
  D_Flip_Flop d_ff_39 ();  // open: clk, D, Q, Qn, preset, reset
  D_Flip_Flop d_ff_40 ();  // open: clk, D, Q, Qn, preset, reset
endmodule
